# Fritzing sketch Vue_PlantinePCB_v3.0 (saved by Fritzing 0.9.10b)
perfboards: 1

parts:
  LCD1 = LCD screen  # not connected
  S1 = Pushbutton [package="[THT]"]
  R1 = Trimmer Potentiometer [maximum_resistance=10kΩ knob_status=50% power=0.5W package=THT]  # not connected
  RHT1 = Humidity and Temperature Sensor RHT03  # not connected
  Mod1 = Amica NodeMCU DEVKIT 1.0  # not connected

nets:
  N1: S1.Pin_1, S1.Pin_2
  N2: S1.Pin_3, S1.Pin_4
